// Digital circuit 77.dig as structural Verilog
module _77 (
  input  in_5,
  input  in_6,
  input  in_7,
  input  in_8,
  input  in_9,
  input  in_10,
  input  in_11,
  input  in_12,
  output S3,
  output S2,
  output S1,
  output s0
);

  wire somador1bit_1_cout, somador1bit_2_cout, somador1bit_3_cout, somador1bit_4_cout;

  LED Overflow (.in(somador1bit_1_cout));
  somador1bit somador1bit_1 (.A(in_5), .B(in_9), .CIn(somador1bit_2_cout), .S(S3), .Cout(somador1bit_1_cout));
  somador1bit somador1bit_2 (.A(in_6), .B(in_10), .CIn(somador1bit_3_cout), .S(S2), .Cout(somador1bit_2_cout));
  Seven_Seg_Hex seven_seg_hex_1 (.d({S3, S2, S1, s0}), .dp(1'b0));
  somador1bit somador1bit_3 (.A(in_7), .B(in_11), .CIn(somador1bit_4_cout), .S(S1), .Cout(somador1bit_3_cout));
  somador1bit somador1bit_4 (.A(in_8), .B(in_12), .CIn(1'b0), .S(s0), .Cout(somador1bit_4_cout));
endmodule
