// Digital circuit ALU.dig as structural Verilog
module ALU (
  input  A0,
  input  A1,
  input  A2,
  input  A3,
  input  B0,
  input  B1,
  input  B2,
  input  B3,
  input  A0_2,
  input  A1_2,
  input  A2_2,
  input  A3_2,
  input  A4,
  input  A5,
  input  A6,
  input  A7,
  input  B0_2,
  input  B1_2,
  input  B2_2,
  input  B3_2,
  input  B4,
  input  B5,
  input  B6,
  input  B7,
  input  A1_3,
  input  A2_3,
  input  A3_3,
  input  A4_2,
  input  A5_2,
  input  A6_2,
  input  A7_2,
  input  A1_4,
  input  A2_4,
  input  A3_4,
  input  A4_3,
  input  A5_3,
  input  A6_3,
  input  A7_3,
  input  A0_3,
  input  B0_3,
  input  A1_5,
  input  B1_3,
  input  A2_5,
  input  B2_3,
  input  A3_5,
  input  B3_3,
  input  A0_4,
  input  A4_4,
  input  B4_2,
  input  A5_4,
  input  B5_2,
  input  A6_4,
  input  B6_2,
  input  A7_4,
  input  B7_2,
  input  B0_4,
  input  A1_6,
  input  B1_4,
  input  A2_6,
  input  B2_4,
  input  A3_6,
  input  B3_4,
  input  A0_5,
  input  A4_5,
  input  B4_3,
  input  A5_5,
  input  B5_3,
  input  A6_5,
  input  B6_3,
  input  A7_5,
  input  B7_3,
  input  B0_5,
  input  A1_7,
  input  B1_5,
  input  A2_7,
  input  B2_5,
  input  A3_7,
  input  B3_5,
  input  A0_6,
  input  A4_6,
  input  B4_4,
  input  A5_6,
  input  B5_4,
  input  A6_6,
  input  B6_4,
  input  A7_6,
  input  B7_4,
  input  A,
  input  B,
  input  A_2,
  input  B_2,
  input  CIn,
  input  A1_8,
  input  A2_8,
  input  A3_8,
  input  A0_7,
  input  B1_6,
  input  B2_6,
  input  B3_6,
  input  B0_6,
  input  A0_8,
  input  A8,
  input  A9,
  input  A10,
  input  A11,
  input  A12,
  input  A13,
  input  A14,
  input  A15,
  input  B8,
  input  B9,
  input  B10,
  input  B11,
  input  B12,
  input  B13,
  input  B14,
  input  B15,
  output S3,
  output S2,
  output S1,
  output s0,
  output COut,
  output S0_2,
  output S1_2,
  output S2_2,
  output s3_2,
  output S4,
  output S5,
  output S6,
  output s7,
  output Overflow,
  output S0_3,
  output S1_3,
  output S2_3,
  output S3_3,
  output S4_2,
  output S5_2,
  output S6_2,
  output S7_2,
  output S0_4,
  output S1_4,
  output S2_4,
  output S3_4,
  output S4_3,
  output S5_3,
  output S5_4,
  output S6_3,
  output Overflow_2,
  output S0_5,
  output S1_5,
  output S2_5,
  output S3_5,
  output S4_4,
  output S5_5,
  output S6_4,
  output S7_3,
  output S0_6,
  output S1_6,
  output S2_6,
  output S3_6,
  output S4_5,
  output S5_6,
  output S6_5,
  output S7_4,
  output S0_7,
  output S1_7,
  output S2_7,
  output S3_7,
  output S4_6,
  output S5_7,
  output S6_6,
  output S7_5,
  output S,
  output COut_2,
  output S8,
  output COut_3,
  output S0_8,
  output S1_8,
  output S2_8,
  output S3_8,
  output S4_7,
  output S5_8,
  output S6_7,
  output S7_6,
  output S9,
  output S10,
  output S11,
  output s8_2,
  output S13,
  output S14,
  output S15,
  output s12,
  output Overflow_3
);

  wire A0_B0, A0_B1, A0_B2, A0_B3, A1_B0, A1_B1, A1_B2, A1_B3, A2_B0, A2_B1, A2_B2, A2_B3, A3_B0, A3_B1,
       A3_B2, A3_B3, and_10_out, and_11_out, B2_t, B4_t, B5_t, B6_t, B7_t, Carry1, Carry2A, Carry2B, carry3A,
       carry3B, carry3C, Carry4A, Carry4B, Carry4C, Carry5A, Carry5B, sFA2, sFA3, sFA4, sFA5, sFA6,
       somador1bit_2_cout, somador1bit_3_cout, somador1bit_4_cout, somador4bits_1_cout, SomaFA1, xor_10_out;

  somador1bit somador1bit_1 (.A(A0), .B(B0), .CIn(somador1bit_2_cout), .S(S3), .Cout(COut));
  somador1bit somador1bit_2 (.A(A1), .B(B1), .CIn(somador1bit_3_cout), .S(S2), .Cout(somador1bit_2_cout));
  somador1bit somador1bit_3 (.A(A2), .B(B2), .CIn(somador1bit_4_cout), .S(S1), .Cout(somador1bit_3_cout));
  somador1bit somador1bit_4 (.A(A3), .B(B3), .CIn(1'b0), .S(s0), .Cout(somador1bit_4_cout));
  somador4bits somador4bits_1 (
    .CIn(1'b0), .A0(A0_2), .A1(A1_2), .A2(A2_2), .A3(A3_2), .B0(B0_2), .B1(B1_2), .B2(B2_2), .B3(B3_2),
    .s0(S0_2), .S1(S1_2), .S2(S2_2), .S3(s3_2), .COut(somador4bits_1_cout));
  somador4bits somador4bits_2 (
    .CIn(somador4bits_1_cout), .A0(A4), .A1(A5), .A2(A6), .A3(A7), .B0(B4), .B1(B5), .B2(B6), .B3(B7),
    .s0(S4), .S1(S5), .S2(S6), .S3(s7), .COut(Overflow));
  OR_DE or_de_1 ();  // open: A, B, OR
  AND_DE and_de_1 ();  // open: A, B, AND
  XOR_DE xor_de_1 ();  // open: A, B, XOR
  multiplicador777 multiplicador777_1 ();  // open: A, B, Multiplicador, CoutMultiplier
  ShiftRight_DE shiftright_de_1 ();  // open: A, ShiftRight
  ShiftLeft_DE shiftleft_de_1 ();  // open: A, ShiftLeft, CoutSL
  not not_1 (B0_6, B8);
  not not_2 (B1_6, B9);
  not not_3 (B2_t, B10);
  not not_4 (B3_6, B11);
  not not_5 (B4_t, B12);
  not not_6 (B5_t, B13);
  not not_7 (B6_t, B14);
  not not_8 (B7_t, B15);
  Somador_8bits somador_8bits_1 (
    .A0(A0_7), .A1(A1_8), .A2(A2_8), .A3(A3_8), .A4(A12), .A5(A13), .A6(A14), .A7(A15), .B0(B0_6), .B1(B1_6),
    .B2(B2_t), .B3(B3_6), .B4(B4_t), .B5(B5_t), .B6(B6_t), .B7(B7_t), .CIn(1'b1), .S0(S9), .S1(S10),
    .S2(S11), .s3(s8_2), .S4(S13), .S5(S14), .S6(S15), .s7(s12), .Overflow(Overflow_3));
  and and_1 (S0_5, A0_4, B0_3);
  and and_2 (S1_5, A1_5, B1_3);
  and and_3 (S2_5, A2_5, B2_3);
  and and_4 (S3_5, A3_5, B3_3);
  and and_5 (S4_4, A4_4, B4_2);
  and and_6 (S5_5, A5_4, B5_2);
  and and_7 (S6_4, A6_4, B6_2);
  and and_8 (S7_3, A7_4, B7_2);
  or or_1 (S0_6, A0_5, B0_4);
  or or_2 (S1_6, A1_6, B1_4);
  or or_3 (S2_6, A2_6, B2_4);
  or or_4 (S3_6, A3_6, B3_4);
  or or_5 (S4_5, A4_5, B4_3);
  or or_6 (S5_6, A5_5, B5_3);
  or or_7 (S6_5, A6_5, B6_3);
  or or_8 (S7_4, A7_5, B7_3);
  xor xor_1 (S0_7, A0_6, B0_5);
  xor xor_2 (S1_7, A1_7, B1_5);
  xor xor_3 (S2_7, A2_7, B2_5);
  xor xor_4 (S3_7, A3_7, B3_5);
  xor xor_5 (S4_6, A4_6, B4_4);
  xor xor_6 (S5_7, A5_6, B5_4);
  xor xor_7 (S6_6, A6_6, B6_4);
  xor xor_8 (S7_5, A7_6, B7_4);
  xor xor_9 (S, A, B);
  and and_9 (COut_2, A, B);
  xor xor_10 (xor_10_out, A_2, B_2);
  and and_10 (and_10_out, A_2, B_2);
  and and_11 (and_11_out, xor_10_out, CIn);
  xor xor_11 (S8, xor_10_out, CIn);
  or or_9 (COut_3, and_10_out, and_11_out);
  and and_12 (A0_B0, A0_7, B0_6);
  and and_13 (A0_B1, A0_7, B1_6);
  and and_14 (A0_B2, A0_7, B2_t);
  and and_15 (A0_B3, A0_7, B3_6);
  and and_16 (A1_B0, A1_8, B0_6);
  and and_17 (A1_B1, A1_8, B1_6);
  and and_18 (A1_B2, A1_8, B2_t);
  and and_19 (A1_B3, A1_8, B3_6);
  and and_20 (A2_B0, A2_8, B0_6);
  and and_21 (A2_B1, A2_8, B1_6);
  and and_22 (A2_B2, A2_8, B2_t);
  and and_23 (A2_B3, A2_8, B3_6);
  and and_24 (A3_B0, A3_8, B0_6);
  and and_25 (A3_B1, A3_8, B1_6);
  and and_26 (A3_B2, A3_8, B2_t);
  and and_27 (A3_B3, A3_8, B3_6);
  halfadder HA1 (.A(A1_B0), .B(A0_B1), .S(S1_8), .COut(Carry1));
  FullAdder FA1 (.A(A2_B0), .B(A1_B1), .CIn(Carry1), .S1(SomaFA1), .COut(Carry2A));
  halfadder HA2 (.A(SomaFA1), .B(A0_B2), .S(S2_8), .COut(Carry2B));
  FullAdder FA2 (.A(A3_B0), .B(A2_B1), .CIn(Carry2A), .S1(sFA2), .COut(carry3A));
  FullAdder FA3 (.A(sFA2), .B(A1_B2), .CIn(Carry2B), .S1(sFA3), .COut(carry3B));
  halfadder HA3 (.A(sFA3), .B(A0_B3), .S(S3_8), .COut(carry3C));
  FullAdder FA4 (.A(A3_B1), .B(A2_B2), .CIn(carry3A), .S1(sFA4), .COut(Carry4A));
  FullAdder FA5 (.A(sFA4), .B(A1_B3), .CIn(carry3B), .S1(sFA5), .COut(Carry4B));
  halfadder HA4 (.A(sFA5), .B(carry3C), .S(S4_7), .COut(Carry4C));
  FullAdder FA6 (.A(A3_B2), .B(A2_B3), .CIn(Carry4A), .S1(sFA6), .COut(Carry5A));
  FullAdder FA7 (.A(sFA6), .B(Carry4B), .CIn(Carry4C), .S1(S5_8), .COut(Carry5B));
  FullAdder FA8 (.A(A3_B3), .B(Carry5A), .CIn(Carry5B), .S1(S6_7), .COut(S7_6));

  assign A8 = A0_7;
  assign A9 = A1_8;
  assign A10 = A2_8;
  assign A11 = A3_8;
  assign Overflow_2 = A7_3;
  assign S0_3 = A1_3;
  assign S0_4 = 1'b0;
  assign S0_8 = A0_7;
  assign S1_3 = A2_3;
  assign S1_4 = A0_3;
  assign S2_3 = A3_3;
  assign S2_4 = A1_4;
  assign S3_3 = A4_2;
  assign S3_4 = A2_4;
  assign S4_2 = A5_2;
  assign S4_3 = A3_4;
  assign S5_2 = A6_2;
  assign S5_3 = A4_3;
  assign S5_4 = A5_3;
  assign S6_2 = A7_2;
  assign S6_3 = A6_3;
  assign S7_2 = 1'b0;

  // Other names for the same wires on the sheet: A0_t = A0_7; A1_t = A1_8; A2_t = A2_8; A3_t = A3_8; A4_t = A12;
  //   A5_t = A13; A6_t = A14; A7_t = A15; B0_t = B0_6; B1_t = B1_6; B3_t = B3_6; carry6s = S7_6; S0_t = S9;
  //   S1_t = S10; s1_t_t = S1_8; S2_t = S11; s2_t_t = S2_8; S3_t = s8_2; s3_t_t = S3_8; S4_t = S13; s4_t_t = S4_7;
  //   S5_t = S14; s5_t_t = S5_8; S6_t = S15; s6_t_t = S6_7; S7_t = s12

  // Notes on the sheet:
  //   Somador de 8 Bits
  //   Subtrator de 8 Bits
  //   Shift Right
  //   Shift Left
  //   Operação AND
  //   Operação OR
  //   Operação XOR
  //   Half-Adder
  //   Full-Adder
  //   A0
  //   0-0
  //   1-0
  //   2-0
  //   3-0
  //   A1
  //   0-1
  //   1-1
  //   2-1
  //   3-1
  //   A2
  //   0-2
  //   1-2
  //   2-2
  //   3-2
  //   A3
  //   0-3
  //   1-3
  //   2-3
  //   3-3
  //   Multiplicador
  //   Carry1
endmodule
