// Digital circuit ALU_CPU.dig as structural Verilog
module ALU_CPU (
  input  [7:0] A,
  input  [7:0] B,
  input  [3:0] F,
  output [7:0] S
);

  wire CoutMulti, COutSL, COutSomador, CoutSUbtrator;
  wire [7:0] AND, Multiplicador, OR, ShiftLeft, ShiftRight, Somador, Subtrator, XOR;

  OR_DE or_de_1 (.A(A), .B(B), .OR(OR));
  AND_DE and_de_1 (.A(A), .B(B), .AND(AND));
  XOR_DE xor_de_1 (.A(A), .B(B), .XOR(XOR));
  ShiftRight_DE shiftright_de_1 (.A(A), .ShiftRight(ShiftRight));
  // ShiftLeft_DE shiftleft_de_1: pin names not known; wires that end beside it: A, ShiftLeft, COutSL
  Subtrator_DE subtrator_de_1 (.A(A), .B(B), .Overflow(CoutSUbtrator), .Subtrator(Subtrator));
  Somador_DE somador_de_1 (.A(A), .B(B), .Overflow(COutSomador), .Somador(Somador));
  multiplicador777 multiplicador777_1 (.A(A), .B(B), .Multiplicador(Multiplicador), .CoutMultiplier(CoutMulti));
  Multiplexer #(.Selector_Bits(4), .Bits(8)) multiplexer_1 (
    .sel(F), .in_0(A), .in_1(OR), .in_2(AND), .in_3(XOR), .in_4(ShiftLeft), .in_5(Subtrator), .in_6(Somador),
    .in_7(ShiftRight), .in_8(Multiplicador), .in_9({8{1'b0}}), .in_10({8{1'b0}}), .in_11({8{1'b0}}),
    .in_12({8{1'b0}}), .in_13({8{1'b0}}), .in_14({8{1'b0}}), .in_15({8{1'b0}}), .out(S));
  Seven_Seg_Hex seven_seg_hex_1 (.d(S[7:4]), .dp(1'b0));
  Seven_Seg_Hex seven_seg_hex_2 (.d(S[3:0]), .dp(1'b0));

  // Other names for the same wires on the sheet: COutSel[7:0] = S; Segundo[3:0] = S[3:0]; Primeiro[3:0] = S[7:4];
  //   Sele[3:0] = F

  // Notes on the sheet:
  //   .
  //   Componentes
  //   Multiplexadores
  //   Terra para Displays
  //   Display para Resultados
  //   Botões para demais operações
  //   Distribuidor para Displays
  //   Seletor de Operações
  //   0 = A
  //   1 = OR
  //   2 = AND
  //   3 = XOR
  //   4 = SHIFT LEFT
  //   5 = SUBTRATOR
  //   6 = SOMADOR
  //   7 = SHIFT RIGHT
  //   8 = MULTIPLICADOR
endmodule
