// Digital circuit CPU.dig as structural Verilog
module CPU (
  input  [2:0] in_1
);

  wire button_1_out;
  wire [3:0] P, S;
  wire [7:0] A, S_ALU;
  wire [10:8] D;

  Button button_1 (.out(button_1_out));
  EEPROMDualPort #(.AddrBits(3), .Bits(11)) eepromdualport_1 (
    .A(in_1), .Din({11{1'b0}}), .str(1'b0), .C(button_1_out), .ld(1'b1), .D({D, A}));
  alu_teste alu_teste_1 (.A(A), .B({S, P}), .F(D), .S(S_ALU));
  Register #(.Bits(8)) register_1 (.D(S_ALU), .C(button_1_out), .en(1'b1), .Q({S, P}));
  Seven_Seg_Hex seven_seg_hex_1 (.d(S), .dp(1'b0));
  Seven_Seg_Hex seven_seg_hex_2 (.d(P), .dp(1'b0));

  // Other names for the same wires on the sheet: A_EEPROM[2:0] = in_1; D[7:0] = A; F_Seletor[2:0] = D

  // Notes on the sheet:
  //   contents of eepromdualport_1 (hex, n*v repeats v):
  //   501,101
endmodule
