// Digital circuit Enable.dig as structural Verilog
module Enable (
  input  Enable,
  input  [7:0] A_B,
  output [7:0] S
);

  and and_1 (S[0], Enable, A_B[0]);
  and and_2 (S[1], Enable, A_B[1]);
  and and_3 (S[2], Enable, A_B[2]);
  and and_4 (S[3], Enable, A_B[3]);
  and and_5 (S[4], Enable, A_B[4]);
  and and_6 (S[5], Enable, A_B[5]);
  and and_7 (S[6], Enable, A_B[6]);
  and and_8 (S[7], Enable, A_B[7]);

  // Other names for the same wires on the sheet: _0 = A_B[0]; _1 = A_B[1]; _2 = A_B[2]; _3 = A_B[3]; _4 = A_B[4];
  //   _5 = A_B[5]; _6 = A_B[6]; _7 = A_B[7]
endmodule
