// Digital circuit FullAdder.dig as structural Verilog
module FullAdder (
  input  A,
  input  B,
  input  CIn,
  output S1,
  output COut
);

  wire and_1_out, and_2_out, xor_1_out;

  and and_1 (and_1_out, A, B);
  xor xor_1 (xor_1_out, A, B);
  and and_2 (and_2_out, xor_1_out, CIn);
  xor xor_2 (S1, xor_1_out, CIn);
  or or_1 (COut, and_1_out, and_2_out);
endmodule
