// Digital circuit MULT_BACKUP.dig as structural Verilog
module MULT_BACKUP (
  input  A0,
  input  A1,
  input  A2,
  input  A3,
  input  B0,
  input  B1,
  input  B2,
  input  B3,
  output S0,
  output S1,
  output S2,
  output S3,
  output S4,
  output S5,
  output S6,
  output S7
);

  wire A0_B1, A0_B2, A0_B3, A1_B0, A1_B1, A1_B2, A1_B3, A2_B0, A2_B1, A2_B2, A2_B3, A3_B0, A3_B1, A3_B2,
       A3_B3, Carry1, Carry2A, Carry2B, carry3A, carry3B, carry3C, Carry4A, Carry4B, Carry4C, Carry5A,
       Carry5B, sFA2, sFA3, sFA4, sFA5, sFA6, SomaFA1;

  and and_1 (S0, A0, B0);
  and and_2 (A0_B1, A0, B1);
  and and_3 (A0_B2, A0, B2);
  and and_4 (A0_B3, A0, B3);
  and and_5 (A1_B0, A1, B0);
  and and_6 (A1_B1, A1, B1);
  and and_7 (A1_B2, A1, B2);
  and and_8 (A1_B3, A1, B3);
  and and_9 (A2_B0, A2, B0);
  and and_10 (A2_B1, A2, B1);
  and and_11 (A2_B2, A2, B2);
  and and_12 (A2_B3, A2, B3);
  and and_13 (A3_B0, A3, B0);
  and and_14 (A3_B1, A3, B1);
  and and_15 (A3_B2, A3, B2);
  and and_16 (A3_B3, A3, B3);
  halfadder HA1 (.A(A1_B0), .B(A0_B1), .S(S1), .COut(Carry1));
  FullAdder FA1 (.A(A2_B0), .B(A1_B1), .CIn(Carry1), .S1(SomaFA1), .COut(Carry2A));
  halfadder HA2 (.A(SomaFA1), .B(A0_B2), .S(S2), .COut(Carry2B));
  FullAdder FA2 (.A(A3_B0), .B(A2_B1), .CIn(Carry2A), .S1(sFA2), .COut(carry3A));
  FullAdder FA3 (.A(sFA2), .B(A1_B2), .CIn(Carry2B), .S1(sFA3), .COut(carry3B));
  halfadder HA3 (.A(sFA3), .B(A0_B3), .S(S3), .COut(carry3C));
  FullAdder FA4 (.A(A3_B1), .B(A2_B2), .CIn(carry3A), .S1(sFA4), .COut(Carry4A));
  FullAdder FA5 (.A(sFA4), .B(A1_B3), .CIn(carry3B), .S1(sFA5), .COut(Carry4B));
  halfadder HA4 (.A(sFA5), .B(carry3C), .S(S4), .COut(Carry4C));
  FullAdder FA6 (.A(A3_B2), .B(A2_B3), .CIn(Carry4A), .S1(sFA6), .COut(Carry5A));
  FullAdder FA7 (.A(sFA6), .B(Carry4B), .CIn(Carry4C), .S1(S5), .COut(Carry5B));
  FullAdder FA8 (.A(A3_B3), .B(Carry5A), .CIn(Carry5B), .S1(S6), .COut(S7));

  // Other names for the same wires on the sheet: A0_B0 = S0; carry6s = S7

  // Notes on the sheet:
  //   A0
  //   0-0
  //   1-0
  //   2-0
  //   3-0
  //   A1
  //   0-1
  //   1-1
  //   2-1
  //   3-1
  //   A2
  //   0-2
  //   1-2
  //   2-2
  //   3-2
  //   A3
  //   0-3
  //   1-3
  //   2-3
  //   3-3
  //   Carry1
endmodule
