// Digital circuit OR_DE.dig as structural Verilog
module OR_DE (
  input  [7:0] A,
  input  [7:0] B,
  output [7:0] OR
);

  OR or_1 (
    .A0(A[0]), .A1(A[1]), .A2(A[2]), .A3(A[3]), .A4(A[4]), .A5(A[5]), .A6(A[6]), .A7(A[7]), .B0(B[0]),
    .B1(B[1]), .B2(B[2]), .B3(B[3]), .B4(B[4]), .B5(B[5]), .B6(B[6]), .B7(B[7]), .S0(OR[0]), .S1(OR[1]),
    .S2(OR[2]), .S3(OR[3]), .S4(OR[4]), .S5(OR[5]), .S6(OR[6]), .S7(OR[7]));

  // Other names for the same wires on the sheet: S0 = OR[0]; S1 = OR[1]; S2 = OR[2]; S3 = OR[3]; S4 = OR[4];
  //   S5 = OR[5]; S6 = OR[6]; S7 = OR[7]

  // Notes on the sheet:
  //   OR: OR
endmodule
