// Digital circuit ShiftLeft_DE.dig as structural Verilog
module ShiftLeft_DE (
  input  [7:0] A,
  output [8:0] ShiftLeft,
  output CoutSL
);

  wire \Saída ;

  shift_left shift_left_1 (
    .A0(A[0]), .A1(A[1]), .A2(A[2]), .A3(A[3]), .A4(A[4]), .A5(A[5]), .A6(A[6]), .A7(A[7]), .S0(CoutSL),
    .S1(ShiftLeft[1]), .S2(ShiftLeft[2]), .S3(ShiftLeft[3]), .S4(ShiftLeft[4]), .S5(ShiftLeft[5]),
    .S6(ShiftLeft[6]), .S7(ShiftLeft[7]), .Overflow(\Saída ));
  // Pins of 8 and 9 bits meet at {ShiftLeft[8:1], CoutSL}

  assign ShiftLeft[0] = CoutSL;

  // Other names for the same wires on the sheet: S0 = CoutSL; S1 = ShiftLeft[1]; S2 = ShiftLeft[2]; S3 = ShiftLeft[3];
  //   S4 = ShiftLeft[4]; S5 = ShiftLeft[5]; S6 = ShiftLeft[6]; S7 = ShiftLeft[7]
endmodule
