// Digital circuit ShiftRight_DE.dig as structural Verilog
module ShiftRight_DE (
  input  [7:0] A,
  output [7:0] ShiftRight
);

  shift_right shift_right_1 (
    .A0(A[0]), .A1(A[1]), .A2(A[2]), .A3(A[3]), .A4(A[4]), .A5(A[5]), .A6(A[6]), .A7(A[7]),
    .S0(ShiftRight[0]), .S1(ShiftRight[1]), .S2(ShiftRight[2]), .S3(ShiftRight[3]), .S4(ShiftRight[4]),
    .S5(ShiftRight[5]), .S6(ShiftRight[6]), .S7(ShiftRight[7]));

  // Other names for the same wires on the sheet: S0 = ShiftRight[0]; S1 = ShiftRight[1]; S2 = ShiftRight[2];
  //   S3 = ShiftRight[3]; S4 = ShiftRight[4]; S5 = ShiftRight[5]; S6 = ShiftRight[6]; S7 = ShiftRight[7]
endmodule
