// Digital circuit Somador1bit_res.dig as structural Verilog
module Somador1bit_res (
  input  A,
  input  B,
  input  CIn,
  output S,
  output COut
);

  wire and_1_out, and_2_out, xor_1_out;

  xor xor_1 (xor_1_out, A, B);
  and and_1 (and_1_out, A, B);
  xor xor_2 (S, CIn, xor_1_out);
  and and_2 (and_2_out, CIn, xor_1_out);
  or or_1 (COut, and_2_out, and_1_out);
endmodule
