// Digital circuit Somador_8bits.dig as structural Verilog
module Somador_8bits (
  input  A0,
  input  A1,
  input  A2,
  input  A3,
  input  A4,
  input  A5,
  input  A6,
  input  A7,
  input  B0,
  input  B1,
  input  B2,
  input  B3,
  input  B4,
  input  B5,
  input  B6,
  input  B7,
  input  CIn,
  output S0,
  output S1,
  output S2,
  output s3,
  output S4,
  output S5,
  output S6,
  output s7,
  output Overflow
);

  wire somador4bits_1_cout;

  somador4bits somador4bits_1 (
    .CIn(CIn), .A0(A0), .A1(A1), .A2(A2), .A3(A3), .B0(B0), .B1(B1), .B2(B2), .B3(B3), .s0(S0), .S1(S1),
    .S2(S2), .S3(s3), .COut(somador4bits_1_cout));
  somador4bits somador4bits_2 (
    .CIn(somador4bits_1_cout), .A0(A4), .A1(A5), .A2(A6), .A3(A7), .B0(B4), .B1(B5), .B2(B6), .B3(B7),
    .s0(S4), .S1(S5), .S2(S6), .S3(s7), .COut(Overflow));
endmodule
