// Digital circuit Somador_DE.dig as structural Verilog
module Somador_DE (
  input  [7:0] A,
  input  [7:0] B,
  output Overflow,
  output [7:0] Somador
);

  wire somador4bits_1_cout;

  somador4bits somador4bits_1 (
    .CIn(1'b0), .A0(A[0]), .A1(A[1]), .A2(A[2]), .A3(A[3]), .B0(B[0]), .B1(B[1]), .B2(B[2]), .B3(B[3]),
    .s0(Somador[0]), .S1(Somador[1]), .S2(Somador[2]), .S3(Somador[3]), .COut(somador4bits_1_cout));
  somador4bits somador4bits_2 (
    .CIn(somador4bits_1_cout), .A0(A[4]), .A1(A[5]), .A2(A[6]), .A3(A[7]), .B0(B[4]), .B1(B[5]), .B2(B[6]),
    .B3(B[7]), .s0(Somador[4]), .S1(Somador[5]), .S2(Somador[6]), .S3(Somador[7]), .COut(Overflow));

  // Other names for the same wires on the sheet: S0 = Somador[0]; S1 = Somador[1]; S2 = Somador[2]; S3 = Somador[3];
  //   S4 = Somador[4]; S5 = Somador[5]; S6 = Somador[6]; S7 = Somador[7]

  // Notes on the sheet:
  //   Somador de 8 Bits
endmodule
