// Digital circuit Subtrator_8bits.dig as structural Verilog
module Subtrator_8bits (
  input  A0,
  input  A1,
  input  A2,
  input  A3,
  input  A4,
  input  A5,
  input  A6,
  input  A7,
  input  B0,
  input  B1,
  input  B2,
  input  B3,
  input  B4,
  input  B5,
  input  B6,
  input  B7,
  output S0,
  output S1,
  output S2,
  output s3,
  output S4,
  output S5,
  output S6,
  output s7,
  output Overflow
);

  wire somador4bits_1_cout, xor_1_out, xor_2_out, xor_3_out, xor_4_out, xor_5_out, xor_6_out, xor_7_out,
       xor_8_out;

  xor xor_1 (xor_1_out, B0, 1'b1);
  xor xor_2 (xor_2_out, B1, 1'b1);
  xor xor_3 (xor_3_out, B2, 1'b1);
  xor xor_4 (xor_4_out, B3, 1'b1);
  xor xor_5 (xor_5_out, B4, 1'b1);
  xor xor_6 (xor_6_out, B5, 1'b1);
  xor xor_7 (xor_7_out, B6, 1'b1);
  xor xor_8 (xor_8_out, B7, 1'b1);
  somador4bits somador4bits_1 (
    .CIn(1'b0), .A0(A0), .A1(A1), .A2(A2), .A3(A3), .B0(xor_1_out), .B1(xor_2_out), .B2(xor_3_out),
    .B3(xor_4_out), .s0(S0), .S1(S1), .S2(S2), .S3(s3), .COut(somador4bits_1_cout));
  somador4bits somador4bits_2 (
    .CIn(somador4bits_1_cout), .A0(A4), .A1(A5), .A2(A6), .A3(A7), .B0(xor_5_out), .B1(xor_6_out),
    .B2(xor_7_out), .B3(xor_8_out), .s0(S4), .S1(S5), .S2(S6), .S3(s7), .COut(Overflow));
endmodule
