// Digital circuit Subtrator_DE.dig as structural Verilog
module Subtrator_DE (
  input  [7:0] A,
  input  [7:0] B,
  output Overflow,
  output [7:0] Subtrator
);

  wire A0, A1, A2, A3, A4, A5, A6, A7;

  Somador_8bits somador_8bits_1 (
    .A0(A0), .A1(A1), .A2(A2), .A3(A3), .A4(A4), .A5(A5), .A6(A6), .A7(A7), .B0(B[0]), .B1(B[1]), .B2(B[2]),
    .B3(B[3]), .B4(B[4]), .B5(B[5]), .B6(B[6]), .B7(B[7]), .CIn(1'b1), .S0(Subtrator[0]), .S1(Subtrator[1]),
    .S2(Subtrator[2]), .s3(Subtrator[3]), .S4(Subtrator[4]), .S5(Subtrator[5]), .S6(Subtrator[6]),
    .s7(Subtrator[7]), .Overflow(Overflow));
  not not_1 (A0, A[0]);
  not not_2 (A1, A[1]);
  not not_3 (A2, A[2]);
  not not_4 (A3, A[3]);
  not not_5 (A4, A[4]);
  not not_6 (A5, A[5]);
  not not_7 (A6, A[6]);
  not not_8 (A7, A[7]);

  // Other names for the same wires on the sheet: S0 = Subtrator[0]; S1 = Subtrator[1]; S2 = Subtrator[2];
  //   S3 = Subtrator[3]; S4 = Subtrator[4]; S5 = Subtrator[5]; S6 = Subtrator[6]; S7 = Subtrator[7]
endmodule
