// Digital circuit XOR_DE.dig as structural Verilog
module XOR_DE (
  input  [7:0] A,
  input  [7:0] B,
  output [7:0] XOR
);

  \xor  xor_1 (
    .A0(A[0]), .A1(A[1]), .A2(A[2]), .A3(A[3]), .A4(A[4]), .A5(A[5]), .A6(A[6]), .A7(A[7]), .B0(B[0]),
    .B1(B[1]), .B2(B[2]), .B3(B[3]), .B4(B[4]), .B5(B[5]), .B6(B[6]), .B7(B[7]), .S0(XOR[0]), .S1(XOR[1]),
    .S2(XOR[2]), .S3(XOR[3]), .S4(XOR[4]), .S5(XOR[5]), .S6(XOR[6]), .S7(XOR[7]));

  // Other names for the same wires on the sheet: S0 = XOR[0]; S1 = XOR[1]; S2 = XOR[2]; S3 = XOR[3]; S4 = XOR[4];
  //   S5 = XOR[5]; S6 = XOR[6]; S7 = XOR[7]
endmodule
