// Digital circuit alu_teste.dig as structural Verilog
module alu_teste (
  input  [7:0] A,
  input  [7:0] B,
  input  [2:0] F,
  output [7:0] S
);

  wire CoutMulti, Couts, COutSL, COutSomador, CoutSUbtrator;
  wire [7:0] AND, Multiplicador, OR, ShiftLeft, ShiftRight, Somador, Subtrator, XOR;

  ShiftRight_DE shiftright_de_1 (.A(A), .ShiftRight(ShiftRight));
  // ShiftLeft_DE shiftleft_de_1: pin names not known; wires that end beside it: A, ShiftLeft, COutSL
  Subtrator_DE subtrator_de_1 (.A(A), .B(B), .Overflow(CoutSUbtrator), .Subtrator(Subtrator));
  Somador_DE somador_de_1 (.A(A), .B(B), .Overflow(COutSomador), .Somador(Somador));
  multiplicador777 multiplicador777_1 (.A(A), .B(B), .Multiplicador(Multiplicador), .CoutMultiplier(CoutMulti));
  OR_DE or_de_1 (.A(A), .B(B), .OR(OR));
  AND_DE and_de_1 (.A(A), .B(B), .AND(AND));
  XOR_DE xor_de_1 (.A(A), .B(B), .XOR(XOR));
  Multiplexer #(.Selector_Bits(3), .Bits(8)) multiplexer_1 (
    .sel(F), .in_0(OR), .in_1(AND), .in_2(XOR), .in_3(ShiftLeft), .in_4(Subtrator), .in_5(Somador),
    .in_6(ShiftRight), .in_7(Multiplicador), .out(S));
  Multiplexer #(.Selector_Bits(3)) multiplexer_2 (
    .sel(F), .in_0(1'b0), .in_1(1'b0), .in_2(COutSL), .in_3(CoutSUbtrator), .in_4(CoutMulti),
    .in_5(CoutSUbtrator), .in_6(1'b0), .in_7(1'b0), .out(Couts));
  LED led_1 (.in(Couts));
  Seven_Seg_Hex seven_seg_hex_1 (.d(S[7:4]), .dp(1'b0));
  Seven_Seg_Hex seven_seg_hex_2 (.d(S[3:0]), .dp(1'b0));

  // Other names for the same wires on the sheet: COutSel[7:0] = S; Segundo[3:0] = S[3:0]; Primeiro[3:0] = S[7:4];
  //   Sele[2:0] = F

  // Notes on the sheet:
  //   .
  //   Componentes
  //   Multiplexadores
  //   Indicador de OverFlow
  //   Terra para Displays
  //   Display para Resultados
  //   Botões para demais operações
  //   Distribuidor para Displays
  //   Seletor de Operações
  //   0 = OR
  //   1 = AND
  //   2 = XOR
  //   3 = SHIFT LEFT
  //   4 = SUBTRATOR
  //   5 = SOMADOR
  //   6 = SHIFT RIGHT
  //   7 = MULTIPLICADOR
endmodule
