// Digital circuit backup.dig as structural Verilog
module backup (
  input  A0,
  input  A1,
  input  A2,
  input  A3,
  input  B0,
  input  B1,
  input  B2,
  input  B3,
  input  A0_2,
  input  A1_2,
  input  A2_2,
  input  A3_2,
  input  A4,
  input  A5,
  input  A6,
  input  A7,
  input  B0_2,
  input  B1_2,
  input  B2_2,
  input  B3_2,
  input  B4,
  input  B5,
  input  B6,
  input  B7,
  input  A0_3,
  input  A1_3,
  input  A2_3,
  input  A3_3,
  input  A4_2,
  input  A5_2,
  input  A6_2,
  input  A7_2,
  input  B0_3,
  input  B1_3,
  input  B2_3,
  input  B3_3,
  input  B4_2,
  input  B5_2,
  input  B6_2,
  input  B7_2,
  input  A1_4,
  input  A2_4,
  input  A3_4,
  input  A4_3,
  input  A5_3,
  input  A6_3,
  input  A7_3,
  input  A1_5,
  input  A2_5,
  input  A3_5,
  input  A4_4,
  input  A5_4,
  input  A6_4,
  input  A7_4,
  input  A0_4,
  input  B0_4,
  input  A1_6,
  input  B1_4,
  input  A2_6,
  input  B2_4,
  input  A3_6,
  input  B3_4,
  input  A0_5,
  input  A4_5,
  input  B4_3,
  input  A5_5,
  input  B5_3,
  input  A6_5,
  input  B6_3,
  input  A7_5,
  input  B7_3,
  input  B0_5,
  input  A1_7,
  input  B1_5,
  input  A2_7,
  input  B2_5,
  input  A3_7,
  input  B3_5,
  input  A0_6,
  input  A4_6,
  input  B4_4,
  input  A5_6,
  input  B5_4,
  input  A6_6,
  input  B6_4,
  input  A7_6,
  input  B7_4,
  input  B0_6,
  input  A1_8,
  input  B1_6,
  input  A2_8,
  input  B2_6,
  input  A3_8,
  input  B3_6,
  input  A0_7,
  input  A4_7,
  input  B4_5,
  input  A5_7,
  input  B5_5,
  input  A6_7,
  input  B6_5,
  input  A7_7,
  input  B7_5,
  input  A,
  input  B,
  output S3,
  output S2,
  output S1,
  output s0,
  output COut,
  output S0_2,
  output S1_2,
  output S2_2,
  output s3_2,
  output S4,
  output S5,
  output S6,
  output s7,
  output Overflow,
  output S0_3,
  output S1_3,
  output S2_3,
  output s3_3,
  output S4_2,
  output S5_2,
  output S6_2,
  output s7_2,
  output Overflow_2,
  output S0_4,
  output S1_4,
  output S2_4,
  output S3_4,
  output S4_3,
  output S5_3,
  output S6_3,
  output S7_3,
  output S0_5,
  output S1_5,
  output S2_5,
  output S3_5,
  output S4_4,
  output S5_4,
  output S5_5,
  output S6_4,
  output Overflow_3,
  output S0_6,
  output S1_6,
  output S2_6,
  output S3_6,
  output S4_5,
  output S5_6,
  output S6_5,
  output S7_4,
  output S0_7,
  output S1_7,
  output S2_7,
  output S3_7,
  output S4_6,
  output S5_7,
  output S6_6,
  output S7_5,
  output S0_8,
  output S1_8,
  output S2_8,
  output S3_8,
  output S4_7,
  output S5_8,
  output S6_7,
  output S7_6,
  output S,
  output COut_2
);

  wire somador1bit_2_cout, somador1bit_3_cout, somador1bit_4_cout, somador4bits_1_cout, somador4bits_3_cout,
       xor_1_out, xor_2_out, xor_3_out, xor_4_out, xor_5_out, xor_6_out, xor_7_out, xor_8_out;

  somador1bit somador1bit_1 (.A(A0), .B(B0), .CIn(somador1bit_2_cout), .S(S3), .Cout(COut));
  somador1bit somador1bit_2 (.A(A1), .B(B1), .CIn(somador1bit_3_cout), .S(S2), .Cout(somador1bit_2_cout));
  somador1bit somador1bit_3 (.A(A2), .B(B2), .CIn(somador1bit_4_cout), .S(S1), .Cout(somador1bit_3_cout));
  somador1bit somador1bit_4 (.A(A3), .B(B3), .CIn(1'b0), .S(s0), .Cout(somador1bit_4_cout));
  somador4bits somador4bits_1 (
    .CIn(1'b0), .A0(A0_2), .A1(A1_2), .A2(A2_2), .A3(A3_2), .B0(B0_2), .B1(B1_2), .B2(B2_2), .B3(B3_2),
    .s0(S0_2), .S1(S1_2), .S2(S2_2), .S3(s3_2), .COut(somador4bits_1_cout));
  somador4bits somador4bits_2 (
    .CIn(somador4bits_1_cout), .A0(A4), .A1(A5), .A2(A6), .A3(A7), .B0(B4), .B1(B5), .B2(B6), .B3(B7),
    .s0(S4), .S1(S5), .S2(S6), .S3(s7), .COut(Overflow));
  xor xor_1 (xor_1_out, B0_3, 1'b1);
  xor xor_2 (xor_2_out, B1_3, 1'b1);
  xor xor_3 (xor_3_out, B2_3, 1'b1);
  xor xor_4 (xor_4_out, B3_3, 1'b1);
  xor xor_5 (xor_5_out, B4_2, 1'b1);
  xor xor_6 (xor_6_out, B5_2, 1'b1);
  xor xor_7 (xor_7_out, B6_2, 1'b1);
  xor xor_8 (xor_8_out, B7_2, 1'b1);
  somador4bits somador4bits_3 (
    .CIn(1'b0), .A0(A0_3), .A1(A1_3), .A2(A2_3), .A3(A3_3), .B0(xor_1_out), .B1(xor_2_out), .B2(xor_3_out),
    .B3(xor_4_out), .s0(S0_3), .S1(S1_3), .S2(S2_3), .S3(s3_3), .COut(somador4bits_3_cout));
  somador4bits somador4bits_4 (
    .CIn(somador4bits_3_cout), .A0(A4_2), .A1(A5_2), .A2(A6_2), .A3(A7_2), .B0(xor_5_out), .B1(xor_6_out),
    .B2(xor_7_out), .B3(xor_8_out), .s0(S4_2), .S1(S5_2), .S2(S6_2), .S3(s7_2), .COut(Overflow_2));
  and and_1 (S0_6, A0_5, B0_4);
  and and_2 (S1_6, A1_6, B1_4);
  and and_3 (S2_6, A2_6, B2_4);
  and and_4 (S3_6, A3_6, B3_4);
  and and_5 (S4_5, A4_5, B4_3);
  and and_6 (S5_6, A5_5, B5_3);
  and and_7 (S6_5, A6_5, B6_3);
  and and_8 (S7_4, A7_5, B7_3);
  or or_1 (S0_7, A0_6, B0_5);
  or or_2 (S1_7, A1_7, B1_5);
  or or_3 (S2_7, A2_7, B2_5);
  or or_4 (S3_7, A3_7, B3_5);
  or or_5 (S4_6, A4_6, B4_4);
  or or_6 (S5_7, A5_6, B5_4);
  or or_7 (S6_6, A6_6, B6_4);
  or or_8 (S7_5, A7_6, B7_4);
  xor xor_9 (S0_8, A0_7, B0_6);
  xor xor_10 (S1_8, A1_8, B1_6);
  xor xor_11 (S2_8, A2_8, B2_6);
  xor xor_12 (S3_8, A3_8, B3_6);
  xor xor_13 (S4_7, A4_7, B4_5);
  xor xor_14 (S5_8, A5_7, B5_5);
  xor xor_15 (S6_7, A6_7, B6_5);
  xor xor_16 (S7_6, A7_7, B7_5);
  // XOr xor_17 has open pins: In_1=open, In_2=open, out=S
  // And and_9 has open pins: In_1=open, In_2=open, out=COut_2

  assign Overflow_3 = A7_4;
  assign S0_4 = A1_4;
  assign S0_5 = 1'b0;
  assign S1_4 = A2_4;
  assign S1_5 = A0_4;
  assign S2_4 = A3_4;
  assign S2_5 = A1_5;
  assign S3_4 = A4_3;
  assign S3_5 = A2_5;
  assign S4_3 = A5_3;
  assign S4_4 = A3_5;
  assign S5_3 = A6_3;
  assign S5_4 = A4_4;
  assign S5_5 = A5_4;
  assign S6_3 = A7_3;
  assign S6_4 = A6_4;
  assign S7_3 = 1'b0;

  // Notes on the sheet:
  //   Somador de 8 Bits
  //   Subtrator de 8 Bits
  //   Shift Right
  //   Shift Left
  //   Operação AND
  //   Operação OR
  //   Operação XOR
endmodule
