// Digital circuit multiplicador777.dig as structural Verilog
module multiplicador777 (
  input  [7:0] A,
  input  [7:0] B,
  output [7:0] Multiplicador,
  output CoutMultiplier
);

  wire A0_B1, A0_B2, A0_B3, A1_B0, A1_B1, A1_B2, A1_B3, A2_B0, A2_B1, A2_B2, A2_B3, A3_B0, A3_B1, A3_B2,
       A3_B3, Carry1, Carry2A, Carry2B, carry3A, carry3B, carry3C, Carry4A, Carry4B, Carry4C, Carry5A,
       Carry5B, sFA2, sFA3, sFA4, sFA5, sFA6, SomaFA1, xor_1_out, xor_2_out;

  and and_1 (Multiplicador[0], A[0], B[0]);
  and and_2 (A0_B1, A[0], B[1]);
  and and_3 (A0_B2, A[0], B[2]);
  and and_4 (A0_B3, A[0], B[3]);
  and and_5 (A1_B0, A[1], B[0]);
  and and_6 (A1_B1, A[1], B[1]);
  and and_7 (A1_B2, A[1], B[2]);
  and and_8 (A1_B3, A[1], B[3]);
  and and_9 (A2_B0, A[2], B[0]);
  and and_10 (A2_B1, A[2], B[1]);
  and and_11 (A2_B2, A[2], B[2]);
  and and_12 (A2_B3, A[2], B[3]);
  and and_13 (A3_B0, A[3], B[0]);
  and and_14 (A3_B1, A[3], B[1]);
  and and_15 (A3_B2, A[3], B[2]);
  and and_16 (A3_B3, A[3], B[3]);
  halfadder HA1 (.A(A1_B0), .B(A0_B1), .S(Multiplicador[1]), .COut(Carry1));
  FullAdder FA1 (.A(A2_B0), .B(A1_B1), .CIn(Carry1), .S1(SomaFA1), .COut(Carry2A));
  halfadder HA2 (.A(SomaFA1), .B(A0_B2), .S(Multiplicador[2]), .COut(Carry2B));
  FullAdder FA2 (.A(A3_B0), .B(A2_B1), .CIn(Carry2A), .S1(sFA2), .COut(carry3A));
  FullAdder FA3 (.A(sFA2), .B(A1_B2), .CIn(Carry2B), .S1(sFA3), .COut(carry3B));
  halfadder HA3 (.A(sFA3), .B(A0_B3), .S(Multiplicador[3]), .COut(carry3C));
  FullAdder FA4 (.A(A3_B1), .B(A2_B2), .CIn(carry3A), .S1(sFA4), .COut(Carry4A));
  FullAdder FA5 (.A(sFA4), .B(A1_B3), .CIn(carry3B), .S1(sFA5), .COut(Carry4B));
  halfadder HA4 (.A(sFA5), .B(carry3C), .S(Multiplicador[4]), .COut(Carry4C));
  FullAdder FA6 (.A(A3_B2), .B(A2_B3), .CIn(Carry4A), .S1(sFA6), .COut(Carry5A));
  FullAdder FA7 (.A(sFA6), .B(Carry4B), .CIn(Carry4C), .S1(Multiplicador[5]), .COut(Carry5B));
  FullAdder FA8 (.A(A3_B3), .B(Carry5A), .CIn(Carry5B), .S1(Multiplicador[6]), .COut(Multiplicador[7]));
  xor xor_1 (xor_1_out, Multiplicador[4], Multiplicador[5]);
  xor xor_2 (xor_2_out, Multiplicador[6], Multiplicador[7]);
  xor xor_3 (CoutMultiplier, xor_1_out, xor_2_out);

  // Other names for the same wires on the sheet: A0_B0 = Multiplicador[0]; carry6s = Multiplicador[7];
  //   CoutMulti = CoutMultiplier; s1 = Multiplicador[1]; s2 = Multiplicador[2]; s3 = Multiplicador[3];
  //   s4 = Multiplicador[4]; s5 = Multiplicador[5]; s6 = Multiplicador[6]

  // Notes on the sheet:
  //   A0
  //   0-0
  //   1-0
  //   2-0
  //   3-0
  //   A1
  //   0-1
  //   1-1
  //   2-1
  //   3-1
  //   A2
  //   0-2
  //   1-2
  //   2-2
  //   3-2
  //   A3
  //   0-3
  //   1-3
  //   2-3
  //   3-3
  //   Carry1
endmodule
