// Digital circuit somador4bits.dig as structural Verilog
module somador4bits (
  input  CIn,
  input  A0,
  input  A1,
  input  A2,
  input  A3,
  input  B0,
  input  B1,
  input  B2,
  input  B3,
  output s0,
  output S1,
  output S2,
  output S3,
  output COut
);

  wire somador1bit_res_2_cout, somador1bit_res_3_cout, somador1bit_res_4_cout;

  Somador1bit_res somador1bit_res_1 (.A(A3), .B(B3), .CIn(somador1bit_res_2_cout), .S(S3), .COut(COut));
  Somador1bit_res somador1bit_res_2 (
    .A(A2), .B(B2), .CIn(somador1bit_res_3_cout), .S(S2), .COut(somador1bit_res_2_cout));
  Somador1bit_res somador1bit_res_3 (
    .A(A1), .B(B1), .CIn(somador1bit_res_4_cout), .S(S1), .COut(somador1bit_res_3_cout));
  Somador1bit_res somador1bit_res_4 (.A(A0), .B(B0), .CIn(CIn), .S(s0), .COut(somador1bit_res_4_cout));
endmodule
