// Digital circuit somador_8bits_nicola.dig as structural Verilog
module somador_8bits_nicola (
  input  [7:0] A,
  input  [7:0] B,
  output [7:0] S,
  output OvF
);

  wire somador1bit_1_cout, somador1bit_2_cout, somador1bit_3_cout, somador1bit_4_cout, somador1bit_5_cout,
       somador1bit_6_cout, somador1bit_7_cout;

  somador1bit somador1bit_1 (.A(A[0]), .B(B[0]), .CIn(1'b0), .S(S[0]), .Cout(somador1bit_1_cout));
  somador1bit somador1bit_2 (.A(A[1]), .B(B[1]), .CIn(somador1bit_1_cout), .S(S[1]), .Cout(somador1bit_2_cout));
  somador1bit somador1bit_3 (.A(A[2]), .B(B[2]), .CIn(somador1bit_2_cout), .S(S[2]), .Cout(somador1bit_3_cout));
  somador1bit somador1bit_4 (.A(A[3]), .B(B[3]), .CIn(somador1bit_3_cout), .S(S[3]), .Cout(somador1bit_4_cout));
  somador1bit somador1bit_5 (.A(A[4]), .B(B[4]), .CIn(somador1bit_4_cout), .S(S[4]), .Cout(somador1bit_5_cout));
  somador1bit somador1bit_6 (.A(A[5]), .B(B[5]), .CIn(somador1bit_5_cout), .S(S[5]), .Cout(somador1bit_6_cout));
  somador1bit somador1bit_7 (.A(A[6]), .B(B[6]), .CIn(somador1bit_6_cout), .S(S[6]), .Cout(somador1bit_7_cout));
  somador1bit somador1bit_8 (.A(A[7]), .B(B[7]), .CIn(somador1bit_7_cout), .S(S[7]), .Cout(OvF));
endmodule
