// Digital circuit subtrator_op.dig as structural Verilog
module subtrator_op (
  input  A0,
  input  A1,
  input  A2,
  input  A3,
  input  A4,
  input  A5,
  input  A6,
  input  A7,
  input  B0,
  input  B1,
  input  B2,
  input  B3,
  input  B4,
  input  B5,
  input  B6,
  input  B7,
  output S0,
  output S1,
  output S2,
  output s3,
  output S4,
  output S5,
  output S6,
  output s7,
  output Overflow
);

  wire B0_t, B1_t, B2_t, B3_t, B4_t, B5_t, B6_t, B7_t;

  not not_1 (B0_t, B0);
  not not_2 (B1_t, B1);
  not not_3 (B2_t, B2);
  not not_4 (B3_t, B3);
  not not_5 (B4_t, B4);
  not not_6 (B5_t, B5);
  not not_7 (B6_t, B6);
  not not_8 (B7_t, B7);
  Somador_8bits somador_8bits_1 (
    .A0(A0), .A1(A1), .A2(A2), .A3(A3), .A4(A4), .A5(A5), .A6(A6), .A7(A7), .B0(B0_t), .B1(B1_t), .B2(B2_t),
    .B3(B3_t), .B4(B4_t), .B5(B5_t), .B6(B6_t), .B7(B7_t), .CIn(1'b1), .S0(S0), .S1(S1), .S2(S2), .s3(s3),
    .S4(S4), .S5(S5), .S6(S6), .s7(s7), .Overflow(Overflow));
endmodule
